# Fritzing sketch gyokuro (saved by Fritzing 0.9.3b)
circuit board: 8.46667cm x 5.64444cm
breadboards: 1

parts:
  R1 = Rotary Potentiometer (Small) [maximum_resistance=50kΩ package=THT]
  R2 = Rotary Potentiometer (Small) [maximum_resistance=50kΩ package=THT]
  LCD1 = LCD screen
  Part1 = Arduino Uno (Rev3)
  U1 = G3VM-61E1 [package=g3vm-61e1]
  DS1 = DS18B20 1-Wire Temperature Sensor [part_number=DS18B20]
  R3 = Resistor [tolerance=±5% resistance=4.7k package=THT]

nets:
  GND: R1.leg1, R2.leg1, LCD1.VSS, LCD1.R/W, LCD1.LED-, Part1.GND, U1.P$3, DS1.GND
  N1: R1.wiper, LCD1.V0
  VDD: R1.leg2, R2.leg2, LCD1.VDD, Part1.5V, U1.P$1, DS1.VDD, R3.Pin_0
  N2: R2.wiper, Part1.A0
  N3: LCD1.RS, Part1.D4
  N4: LCD1.E, Part1.D6_PWM
  N5: LCD1.DB4, Part1.D10_PWM/SS
  N6: LCD1.DB5, Part1.D11_PWM/MOSI
  N7: LCD1.DB6, Part1.D12/MISO
  N8: LCD1.DB7, Part1.D13/SCK
  N9: LCD1.LED+, Part1.3V3
  N10: Part1.D8, U1.P$2
  N11: Part1.D2, DS1.DQ, R3.Pin_1
